# Fritzing sketch Final Project Schematic (saved by Fritzing 0.9.3b)
breadboards: 1

parts:
  Part1 = Arduino Uno (Rev3)
  Part2 = Real Time Clock Module - DS1307 RTC Breakout Board
  Flow_Meter = mystery part, 3 pins [chip_label=?]
  D1 = Diode [package=diode-hv]
  Power_plug1 = Power plug
  R1 = Resistor [tolerance=±5% resistance=10k package=THT]
  Q2 = MOSFET-NCHANNEL [package=to-92]
  RELAY1 = CAR RELAY [part_number=NVF4-2 package=THT]
  Solenoid = Solenoid

nets:
  N1: Part1.A3, Part2.GND
  N2: Part1.A4/SDA, Part2.SQW
  N3: Part1.A5/SCL, Part2.SCL
  N4: Part1.D12/MISO, Q2.G
  N5: Part1.D2, Flow_Meter.pin3
  N6: Part1.5V, Flow_Meter.pin1
  N7: Flow_Meter.pin2, D1.C
  N8: Power_plug1.VCC, RELAY1.87
  N9: Power_plug1.GND, Solenoid.pin2
  N10: R1.Pin_0, RELAY1.30
  N11: R1.Pin_1, Q2.D
  N12: RELAY1.87A, Solenoid.pin1
