# Fritzing sketch Servo_2_LDR (saved by Fritzing 0.9.3b)
breadboards: 1

parts:
  Part1 = Arduino Uno (Rev3)
  J1 = Basic Servo
  R1 = Photocell (LDR) [package=THT]
  R2 = Photocell (LDR) [package=THT]
  R3 = Resistor [tolerance=±5% resistance=220 package=THT]
  R4 = Resistor [tolerance=±5% resistance=220 package=THT]

nets:
  N1: Part1.A0, R2.pin_0, R4.Pin_1
  N2: Part1.A1, R1.pin_1, R3.Pin_1
  GND: Part1.GND, J1.gnd, R3.Pin_0, R4.Pin_0
  N3: Part1.D7, J1.pulse
  5V: Part1.5V, J1.vcc, R1.pin_0, R2.pin_1

notes:
  a schematic showing two light sensors and a servo motor.
